# Fritzing sketch BlinkyBike (saved by Fritzing 0.9.2b)
stripboards: 1

parts:
  U1 = attiny85 [package=dip]
  J-Power = male pin header, 2 pins [form="♂ (male)"]
  J-Right = male pin header, 2 pins [form="♂ (male)"]
  R2 = Resistor [tolerance=±5% resistance=330 package=THT]
  R4 = Resistor [tolerance=±5% resistance=10k package=THT]
  R5 = Resistor [tolerance=±5% resistance=10k package=THT]
  J-Left = male pin header, 2 pins [form="♂ (male)"]
  R6 = Resistor [tolerance=±5% resistance=330 package=THT]
  J-Front = male pin header, 3 pins [form="♂ (male)"]
  J-Back = male pin header, 4 pins [form="♂ (male)"]
  R1 = Resistor [tolerance=±5% resistance=10k package=THT]
  R3 = Resistor [tolerance=±5% resistance=330 package=THT]
  C1 = Ceramic Capacitor [capacitance=10µF voltage=6.3V package="100 mil [THT, multilayer]"]
  NEOPIXEL_FRONT = Neopixel Strip -- Black (30/m)
  NEOPIXEL_REAR_RIGHT = Neopixel Strip -- Black (30/m)
  NEOPIXEL4_REAR_LEFT = Neopixel Strip -- Black (30/m)
  C4 = Electrolytic Capacitor [capacitance=1µF package="100 mil [THT, electrolytic]"]
  U2 = Battery Holders [package=lipo-1100mAh]

nets:
  N1: U1.Pin_1, R1.Pin_1, C1.1
  N2: U1.Pin_2, R5.Pin_1, J-Left.pin1
  N3: U1.Pin_3, R6.Pin_0
  GND: U1.Pin_4, J-Power.pin2, J-Right.pin2, J-Left.pin2, J-Front.pin3, J-Back.pin4, C1.0, NEOPIXEL_FRONT.GND, NEOPIXEL_REAR_RIGHT.GND, NEOPIXEL4_REAR_LEFT.GND, C4.-, U2.-
  N4: U1.Pin_5, R2.Pin_0
  N5: U1.Pin_6, R3.Pin_0
  N6: U1.Pin_7, J-Right.pin1, R4.Pin_1
  5V: U1.Pin_8, J-Power.pin1, R4.Pin_0, R5.Pin_0, J-Front.pin1, J-Back.pin1, R1.Pin_0, NEOPIXEL_FRONT.+5V, NEOPIXEL_REAR_RIGHT.+5V, NEOPIXEL4_REAR_LEFT.+5V, C4.+, U2.+
  N7: R2.Pin_1, J-Back.pin2, NEOPIXEL4_REAR_LEFT.DI
  N8: R6.Pin_1, J-Front.pin2, NEOPIXEL_FRONT.DI
  N9: J-Back.pin3, R3.Pin_1, NEOPIXEL_REAR_RIGHT.DI

notes:
  Front Light
  Rear Left Light
  Rear Right Light
  5V Power Bank

custom parts:
  Neopixel Strip -- Black (30/m): Neopixel Strip, Black, 30 pixels per meter.
